# Fritzing sketch esp8266_LED_fritzing_sketch (saved by Fritzing 0.9.3b)
breadboards: 1

parts:
  Part1 = FTDI Basic Programmer
  R1 = Resistor [tolerance=±5% resistance=330 package=THT]
  LED1 = LED - 5mm [color="Red (633nm)" package="5 mm [THT]"]
  U1 = ESP8266 WiFi Module [part_number=ESP8266]
  YwRobot_Power_Supply1 = YwRobot Breadboard Power Supply [part_number=545043]

nets:
  N1: Part1.GND, YwRobot_Power_Supply1.GND#13, YwRobot_Power_Supply1.GND#14
  N2: R1.Pin_0, YwRobot_Power_Supply1.GND#11, YwRobot_Power_Supply1.GND#12
  N3: R1.Pin_1, LED1.cathode
  N4: LED1.anode, U1.GPIO_2
  N5: U1.RST, U1.CH_PD, YwRobot_Power_Supply1.VCC#9, YwRobot_Power_Supply1.VCC#10
  N6: YwRobot_Power_Supply1.VCC#5, YwRobot_Power_Supply1.VCC#6

notes:
  CHPD
  RST
  VCC
  GND
  RXD
  TXD
  Set power supply
  to 3.3 V
  ESP8266
  VCC --> +3.3V
  RST --> +3.3V
  CHPD --> +3.3V
  GP2 --> LED (long)
  GND --> GND
  RXD --> TX
  TXD --> RX
  3.3 V Only
  FTDI Adapter
  GND --> GND
  RX --> TDX
  TX --> RDX
  GP2
  LED
  Long --> GP2
  Short --> GND
  (thru resistor)

custom parts:
  ESP8266 WiFi Module: Generic WiFi Module based on the ESP8266 with onboard PCB antenna and UART communications
  YwRobot Breadboard Power Supply: The YwRobot Breadboard Power Supply (MB-V2) has two power rails; they can be 5V or 3V3. Power to the module can be provided through the female USB socket or through the A10 (female) 2.1mm power jack.
