# Fritzing sketch esp8266_pwr_fritzing_sketch (saved by Fritzing 0.9.2b)
breadboards: 1

parts:
  YwRobot_Power_Supply1 = YwRobot Breadboard Power Supply [part_number=545043]
  part = ESP8266 WiFi Module [part_number=ESP8266]
  Part1 = FTDI Basic Programmer

nets:
  N1: YwRobot_Power_Supply1.VCC#10, part.VCC, part.RST, part.CH_PD
  GND: YwRobot_Power_Supply1.GND#14, part.GND, Part1.GND
  N2: part.RXD, Part1.TXO
  N3: part.TXD, Part1.RXI

notes:
  CHPD
  RST
  VCC
  GND
  RXD
  TXD
  Set power supply
  to 3.3 V
  ESP8266
  VCC --> +3.3V
  RST --> +3.3V
  CHPD --> +3.3V
  GND --> GND
  RXD --> TX
  TXD --> RX
  3.3 V Only
  FTDI Adapter
  GND --> GND
  RX --> TDX
  TX --> RDX

custom parts:
  YwRobot Breadboard Power Supply: The YwRobot Breadboard Power Supply (MB-V2) has two power rails; they can be 5V or 3V3. Power to the module can be provided through the female USB socket or through the A10 (female) 2.1mm power jack.
  ESP8266 WiFi Module: Generic WiFi Module based on the ESP8266 with onboard PCB antenna and UART communications
